// Logisim project 8bitcomputer.circ as structural Verilog: 6 circuits, main circuit main
module main (
  input  WR,
  input  ENABLE,
  input  in_3,
  input  in_4,
  input  Manual,
  input  [3:0] in_6,
  input  Load_Read,
  input  SEL,
  input  SUB,
  input  ENABLE_2,
  input  in_11,
  input  WR_2,
  input  ENABLE_3,
  input  [7:0] in_14,
  input  in_15,
  input  ENABLE_4,
  input  [7:0] in_17
);

  wire and_1_out, and_2_out, CLK, not_1_out, not_2_out, not_3_out, not_4_out;
  wire [3:0] Add, controlled_buffer_1_out;
  wire [7:0] ALUOUT, AOUT, B, BOUT, I_p_RAM;

  assign controlled_buffer_1_out = not_1_out ? B[3:0] : 4'bz;  // Controlled_Buffer controlled_buffer_1
  not not_1 (not_1_out, Manual);
  assign controlled_buffer_1_out = Manual ? in_6 : 4'bz;  // Controlled_Buffer controlled_buffer_2
  assign I_p_RAM = and_1_out ? in_14 : 8'bz;  // Controlled_Buffer controlled_buffer_3
  and and_1 (and_1_out, Manual, not_2_out);
  not not_2 (not_2_out, Load_Read);
  assign B = Load_Read ? I_p_RAM : 8'bz;  // Controlled_Buffer controlled_buffer_4
  reg_built_in reg_built_in_1 (.in_1(controlled_buffer_1_out), .in_2(in_3), .in_3(in_11), .in_4(CLK), .out_5(Add));
  assign I_p_RAM = and_2_out ? B : 8'bz;  // Controlled_Buffer controlled_buffer_5
  and and_2 (and_2_out, not_3_out, not_4_out);
  not not_3 (not_3_out, Manual);
  not not_4 (not_4_out, Load_Read);
  LED led_1 (.in(B[7]));
  RAM #(.addrWidth(4)) ram_1 (.addr(Add), .data(I_p_RAM), .sel(SEL), .clk(CLK), .ld(Load_Read), .clr(in_11));
  LED led_2 (.in(B[4]));
  LED led_3 (.in(B[3]));
  LED led_4 (.in(B[5]));
  LED led_5 (.in(B[6]));
  assign B = ENABLE_4 ? in_17 : 8'bz;  // Controlled_Buffer controlled_buffer_6
  LED led_6 (.in(B[2]));
  LED led_7 (.in(B[1]));
  LED led_8 (.in(B[0]));
  Clock clock_1 (.out(CLK));
  alu_main alu_main_1 (.SUB(SUB), .EN(ENABLE_2), .in_3(BOUT), .in_4(AOUT), .Result(B), .Result_2(ALUOUT));
  // _1bitregister 1bitregister_1: pin names not known; wires that end beside it: in_4, AOUT
  // _1bitregister 1bitregister_2: pin names not known; wires that end beside it: in_15, BOUT
  LED led_9 (.in(AOUT[7]));
  LED led_10 (.in(BOUT[7]));
  LED led_11 (.in(AOUT[3]));
  LED led_12 (.in(AOUT[6]));
  LED led_13 (.in(AOUT[4]));
  LED led_14 (.in(AOUT[5]));
  LED led_15 (.in(BOUT[4]));
  LED led_16 (.in(BOUT[6]));
  LED led_17 (.in(BOUT[5]));
  LED led_18 (.in(BOUT[3]));
  LED led_19 (.in(AOUT[2]));
  LED led_20 (.in(AOUT[0]));
  LED led_21 (.in(AOUT[1]));
  LED led_22 (.in(ALUOUT[5]));
  LED led_23 (.in(ALUOUT[4]));
  LED led_24 (.in(ALUOUT[7]));
  LED led_25 (.in(ALUOUT[6]));
  LED led_26 (.in(BOUT[2]));
  LED led_27 (.in(BOUT[1]));
  LED led_28 (.in(BOUT[0]));
  LED led_29 (.in(ALUOUT[3]));
  LED led_30 (.in(ALUOUT[0]));
  LED led_31 (.in(ALUOUT[2]));
  LED led_32 (.in(ALUOUT[1]));

  // Other names for the same wires on the sheet: B1[3:0] = B[3:0]; B2[3:0] = B[7:4]; CLR_A = in_4; CLR_B = in_15;
  //   CLR_R = in_11; L_R = Load_Read; M_A = Manual

  // Notes on the sheet:
  //   BUS
  //   INPUT
  //   FIRST 4 
  //   NEXT 4
  //   REGISTER A
  //   REGISTER B
endmodule

module full__adder (
  input  A,
  input  B,
  input  Cin,
  output S,
  output Co
);

  wire and_1_out, and_2_out, and_3_out, and_4_out, and_5_out, and_6_out, not_1_out, not_2_out, not_3_out,
       not_4_out, or_1_out;

  not not_1 (not_1_out, B);
  not not_2 (not_2_out, A);
  and and_1 (and_1_out, not_1_out, A);
  and and_2 (and_2_out, B, not_2_out);
  or or_1 (or_1_out, and_1_out, and_2_out);
  and and_3 (and_3_out, A, B);
  not not_3 (not_3_out, Cin);
  not not_4 (not_4_out, or_1_out);
  and and_4 (and_4_out, Cin, or_1_out);
  and and_5 (and_5_out, not_3_out, or_1_out);
  and and_6 (and_6_out, not_4_out, Cin);
  or or_2 (Co, and_4_out, and_3_out);
  or or_3 (S, and_5_out, and_6_out);

  // Notes on the sheet:
  //   A
  //   B
  //   Cin
  //   S
  //   Co
endmodule

module _4_b (
  input  in_1,
  input  in_2,
  input  in_3,
  input  in_4,
  input  in_5,
  input  B0,
  input  in_7,
  input  in_8,
  input  in_9,
  output out_10,
  output out_11,
  output out_12,
  output out_13,
  output out_14
);

  wire and_1_out, and_4_out, and_5_out, and_6_out, and_9_out, and_10_out, and_11_out, and_12_out, and_13_out,
       and_14_out, C0, C1, C2, G0, G1, G2, G3, P0, P1, P2, P3;

  and and_1 (and_1_out, P0, in_5);
  xor xor_1 (P0, in_1, B0);
  xor xor_2 (P1, in_2, in_7);
  and and_2 (G0, in_1, B0);
  and and_3 (G1, in_2, in_7);
  or or_1 (C0, and_1_out, G0);
  and and_4 (and_4_out, in_5, P2, P0, P1);
  and and_5 (and_5_out, P1, P2, G0);
  and and_6 (and_6_out, P2, G1);
  or or_2 (C2, and_4_out, G2, and_6_out, and_5_out);
  xor xor_3 (P2, in_3, in_8);
  xor xor_4 (P3, in_4, in_9);
  and and_7 (G2, in_3, in_8);
  and and_8 (G3, in_4, in_9);
  and and_9 (and_9_out, P0, P1, in_5);
  and and_10 (and_10_out, P1, G0);
  and and_11 (and_11_out, in_5, P0, P1, P2, P3);
  and and_12 (and_12_out, P3, P2, P1, G0);
  and and_13 (and_13_out, P3, P2, G1);
  and and_14 (and_14_out, P3, G2);
  or or_3 (C1, and_9_out, G1, and_10_out);
  or or_4 (out_14, G3, and_11_out, and_12_out, and_13_out, and_14_out);
  full__adder full_adder_1 (.A(in_1), .B(B0), .Cin(in_5), .S(out_10));  // open: Co
  full__adder full_adder_2 (.A(in_4), .B(in_9), .Cin(C2), .S(out_13));  // open: Co
  full__adder full_adder_3 (.A(in_2), .B(in_7), .Cin(C0), .S(out_11));  // open: Co
  full__adder full_adder_4 (.A(in_3), .B(in_8), .Cin(C1), .S(out_12));  // open: Co

  // Other names for the same wires on the sheet: A0 = in_1; A1 = in_2; A2 = in_3; A3 = in_4; B1 = in_7; B2 = in_8;
  //   B3 = in_9; Cin = in_5; Cout = out_14; S0 = out_10; S1 = out_11; S2 = out_12; S3 = out_13

  // Notes on the sheet:
  //   C0
  //   C2
  //   generating variables
  //   C1
  //   Cout
  //   FOR BIT 0
  //   FOR BIT 3
  //   Predicting Carries
  //   Implementation
  //   FOR BIT 1
  //   FOR BIT 2
endmodule

module alu_main (
  input  SUB,
  input  EN,
  input  [7:0] in_3,
  input  [7:0] in_4,
  output [7:0] Result,
  output [7:0] Result_2
);

  wire n4_b_1_out_14, xor_1_out, xor_2_out, xor_3_out, xor_4_out, xor_5_out, xor_6_out, xor_7_out, xor_8_out;

  xor xor_1 (xor_1_out, in_3[0], SUB);
  xor xor_2 (xor_2_out, in_3[1], SUB);
  xor xor_3 (xor_3_out, in_3[2], SUB);
  xor xor_4 (xor_4_out, in_3[3], SUB);
  xor xor_5 (xor_5_out, in_3[4], SUB);
  xor xor_6 (xor_6_out, in_3[5], SUB);
  xor xor_7 (xor_7_out, in_3[6], SUB);
  xor xor_8 (xor_8_out, in_3[7], SUB);
  _4_b u_4_b_1 (
    .in_1(in_4[0]), .in_2(in_4[1]), .in_3(in_4[2]), .in_4(in_4[3]), .B0(xor_1_out), .in_7(xor_2_out),
    .in_8(xor_3_out), .in_9(xor_4_out), .out_10(Result_2[0]), .out_11(Result_2[1]), .out_12(Result_2[2]),
    .out_13(Result_2[3]), .out_14(n4_b_1_out_14), .in_5(SUB));
  _4_b u_4_b_2 (
    .in_1(in_4[4]), .in_2(in_4[5]), .in_3(in_4[6]), .in_4(in_4[7]), .B0(xor_5_out), .in_7(xor_6_out),
    .in_8(xor_7_out), .in_9(xor_8_out), .out_10(Result_2[4]), .out_11(Result_2[5]), .out_12(Result_2[6]),
    .out_13(Result_2[7]), .in_5(n4_b_1_out_14));  // open: out_14
  assign Result[0] = EN ? Result_2[0] : 1'bz;  // Controlled_Buffer controlled_buffer_1
  assign Result[1] = EN ? Result_2[1] : 1'bz;  // Controlled_Buffer controlled_buffer_2
  assign Result[2] = EN ? Result_2[2] : 1'bz;  // Controlled_Buffer controlled_buffer_3
  assign Result[3] = EN ? Result_2[3] : 1'bz;  // Controlled_Buffer controlled_buffer_4
  assign Result[4] = EN ? Result_2[4] : 1'bz;  // Controlled_Buffer controlled_buffer_5
  assign Result[5] = EN ? Result_2[5] : 1'bz;  // Controlled_Buffer controlled_buffer_6
  assign Result[6] = EN ? Result_2[6] : 1'bz;  // Controlled_Buffer controlled_buffer_7
  assign Result[7] = EN ? Result_2[7] : 1'bz;  // Controlled_Buffer controlled_buffer_8

  // Other names for the same wires on the sheet: ENABLE = EN

  // Notes on the sheet:
  //   REGISTER B
  //   REGISTER A
  //   ALU
  //   RESULT
endmodule

module ram (
  input  [3:0] in_1,
  input  in_2,
  input  WR,
  input  EN,
  input  in_5,
  input  in_6,
  input  [7:0] in_7,
  output [7:0] BUS
);

  wire A0, A1, A2, A3, and_1_out, and_3_out, and_6_out, and_13_out, and_15_out, and_17_out, and_20_out,
       and_22_out, and_24_out, and_28_out, and_30_out, and_33_out, and_40_out, and_42_out, and_44_out,
       and_46_out, minus_A0, minus_A1, minus_A2, minus_A3, n1bitregister_1_p3, X0, X1, X2, X3, X4, X5, X6,
       X7, X8, X9, X10, X11, X12, X13, X14, X15, Y0, Y1, Y2, Y3, Y4, Y5, Y6, Y7, Y8, Y9, Y10, Y11, Y12, Y13,
       Y14, Y15;

  assign BUS = in_6 ? in_7 : 8'bz;  // Controlled_Buffer controlled_buffer_1
  // _1bitregister 1bitregister_1: pin names not known; wires that end beside it: in_5, BUS, n1bitregister_1_p3
  and and_1 (and_1_out, minus_A0, minus_A1, minus_A2, minus_A3);
  and and_2 (X0, WR, and_1_out);
  and and_3 (and_3_out, A0, minus_A1, A2, minus_A3);
  and and_4 (Y5, and_3_out, EN);
  and and_5 (X5, WR, and_3_out);
  and and_6 (and_6_out, minus_A0, A1, minus_A2, A3);
  and and_7 (X10, WR, and_6_out);
  and and_8 (Y10, and_6_out, EN);
  assign {A3, A2, A1, A0} = in_2 ? in_1 : 4'bz;  // Controlled_Buffer controlled_buffer_2
  // _1bitregister 1bitregister_2: pin names not known; wires that end beside it: in_5, BUS, n1bitregister_1_p3
  and and_9 (X1, WR, and_13_out);
  and and_10 (Y0, and_1_out, EN);
  and and_11 (X6, WR, and_15_out);
  and and_12 (X11, WR, and_17_out);
  and and_13 (and_13_out, A0, minus_A1, minus_A2, minus_A3);
  and and_14 (Y1, and_13_out, EN);
  and and_15 (and_15_out, minus_A0, A1, A2, minus_A3);
  and and_16 (Y6, and_15_out, EN);
  and and_17 (and_17_out, A0, A1, minus_A2, A3);
  and and_18 (Y11, and_17_out, EN);
  // _1bitregister 1bitregister_3: pin names not known; wires that end beside it: in_5, BUS, n1bitregister_1_p3
  and and_19 (X2, WR, and_24_out);
  and and_20 (and_20_out, A0, A1, A2, minus_A3);
  and and_21 (X7, WR, and_20_out);
  and and_22 (and_22_out, minus_A0, minus_A1, A2, A3);
  and and_23 (X12, WR, and_22_out);
  not not_1 (minus_A0, A0);
  not not_2 (minus_A1, A1);
  not not_3 (minus_A2, A2);
  not not_4 (minus_A3, A3);
  // _1bitregister 1bitregister_4: pin names not known; wires that end beside it: in_5, BUS, n1bitregister_1_p3
  and and_24 (and_24_out, minus_A0, A1, minus_A2, minus_A3);
  and and_25 (Y2, and_24_out, EN);
  and and_26 (Y7, and_20_out, EN);
  and and_27 (Y12, and_22_out, EN);
  // _1bitregister 1bitregister_5: pin names not known; wires that end beside it: in_5, BUS, n1bitregister_1_p3
  and and_28 (and_28_out, A0, A1, minus_A2, minus_A3);
  and and_29 (X3, WR, and_28_out);
  and and_30 (and_30_out, minus_A0, minus_A1, minus_A2, A3);
  and and_31 (X8, WR, and_30_out);
  and and_32 (Y8, and_30_out, EN);
  and and_33 (and_33_out, A0, minus_A1, A2, A3);
  and and_34 (X13, WR, and_33_out);
  and and_35 (Y13, and_33_out, EN);
  and and_36 (X4, WR, and_40_out);
  and and_37 (Y3, and_28_out, EN);
  and and_38 (X9, WR, and_42_out);
  and and_39 (X14, WR, and_44_out);
  // _1bitregister 1bitregister_6: pin names not known; wires that end beside it: in_5, BUS, n1bitregister_1_p3
  and and_40 (and_40_out, minus_A0, minus_A1, A2, minus_A3);
  and and_41 (Y4, and_40_out, EN);
  and and_42 (and_42_out, A0, minus_A1, minus_A2, A3);
  and and_43 (Y9, and_42_out, EN);
  and and_44 (and_44_out, minus_A0, A1, A2, A3);
  and and_45 (Y14, and_44_out, EN);
  // _1bitregister 1bitregister_7: pin names not known; wires that end beside it: in_5, BUS, n1bitregister_1_p3
  and and_46 (and_46_out, A0, A1, A2, A3);
  and and_47 (X15, WR, and_46_out);
  // _1bitregister 1bitregister_8: pin names not known; wires that end beside it: in_5, BUS, n1bitregister_1_p3
  and and_48 (Y15, and_46_out, EN);
  // _1bitregister 1bitregister_9: pin names not known; wires that end beside it: in_5, BUS, n1bitregister_1_p3
  // _1bitregister 1bitregister_10: pin names not known; wires that end beside it: in_5, BUS, n1bitregister_1_p3
  // _1bitregister 1bitregister_11: pin names not known; wires that end beside it: in_5, BUS, n1bitregister_1_p3
  // _1bitregister 1bitregister_12: pin names not known; wires that end beside it: in_5, BUS, n1bitregister_1_p3
  // _1bitregister 1bitregister_13: pin names not known; wires that end beside it: in_5, BUS, n1bitregister_1_p3
  // _1bitregister 1bitregister_14: pin names not known; wires that end beside it: in_5, BUS, n1bitregister_1_p3
  // _1bitregister 1bitregister_15: pin names not known; wires that end beside it: in_5, BUS, n1bitregister_1_p3
  // _1bitregister 1bitregister_16: pin names not known; wires that end beside it: in_5, BUS
  Clock clock_1 (.out(n1bitregister_1_p3));

  // Notes on the sheet:
  //   BUS
  //   ADRESS INPUT 
  //   BITS INPUT 
  //   GENERATING VARIABLES
  //   READ IN REGISTER
  //   WRITE IN REGISTER
endmodule

module reg_built_in (
  input  [3:0] in_1,
  input  in_2,
  input  in_3,
  input  in_4,
  output [3:0] out_5
);

  Register #(.width(4)) register_1 (.D(in_1), .en(in_2), .Q(out_5), .clk(in_4), .clr(in_3));
endmodule
